// Logisim project LogicalCircuits.circ as structural Verilog: 11 circuits, main circuit main
module main (
  input  Preset,
  input  Data,
  input  Clear,
  input  A,
  output Q,
  output Not_Q,
  output Q_glitch
);

  wire clock_1_out, not_1_out;

  Clock clock_1 (.out(clock_1_out));
  // Rv32im rv32im_1: pin names not known
  D_Flip_Flop d_ff_1 (.D(Data), .clk(clock_1_out), .Q(Q), .Qn(Not_Q), .preset(Preset), .reset(Clear));
  and and_1 (Q_glitch, A, not_1_out);
  not not_1 (not_1_out, A);
  // Socmem #(.MemSize(26)) socmem_1: pin names not known
  // SocVga socvga_1: pin names not known
endmodule

module BitwiseLogicUnit (
  input  [3:0] A,
  input  [1:0] S,
  input  [3:0] B,
  output [3:0] out_4
);

  wire [3:0] and_1_out, not_1_out, or_1_out, xor_1_out;

  assign not_1_out = ~A;  // NOT_Gate not_1, 4 bits wide
  assign and_1_out = A & B;  // AND_Gate and_1, 4 bits wide
  assign or_1_out = A | B;  // OR_Gate or_1, 4 bits wide
  assign xor_1_out = A ^ B;  // XOR_Gate xor_1, 4 bits wide
  Multiplexer #(.select(2), .width(4)) multiplexer_1 (
    .in0(and_1_out), .in1(or_1_out), .in2(xor_1_out), .in3(not_1_out), .out(out_4), .sel(S));
endmodule

module OneBitComparator (
  input  A,
  input  B,
  output A_gt_B,
  output A_lt_B,
  output A_eq_B
);

  wire not_1_out, not_2_out;

  not not_1 (not_1_out, B);
  not not_2 (not_2_out, A);
  and and_1 (A_gt_B, A, not_1_out);
  and and_2 (A_lt_B, not_2_out, B);
  xnor xnor_1 (A_eq_B, A, B);
endmodule

module OneBitShifter (
  input  A0,
  input  Shift_In,
  input  Shift_Enable,
  output Q0
);

  Multiplexer multiplexer_1 (.in0(A0), .in1(Shift_In), .out(Q0), .sel(Shift_Enable));
endmodule

module FourBitRightShifter (
  input  [3:0] A,
  input  Shift_Enable,
  output [3:0] Q
);

  Multiplexer multiplexer_1 (.in0(A[0]), .in1(A[1]), .out(Q[0]), .sel(Shift_Enable));
  Multiplexer multiplexer_2 (.in0(A[1]), .in1(A[2]), .out(Q[1]), .sel(Shift_Enable));
  Multiplexer multiplexer_3 (.in0(A[2]), .in1(A[3]), .out(Q[2]), .sel(Shift_Enable));
  Multiplexer multiplexer_4 (.in0(A[3]), .in1(1'b0), .out(Q[3]), .sel(Shift_Enable));
endmodule

module Shift_Stage (
  input  [3:0] Data_In,
  input  Shift_Enable,
  output [3:0] Data_Out
);

  Multiplexer multiplexer_1 (.in0(Data_In[0]), .in1(Data_In[1]), .out(Data_Out[0]), .sel(Shift_Enable));
  Multiplexer multiplexer_2 (.in0(Data_In[1]), .in1(Data_In[2]), .out(Data_Out[1]), .sel(Shift_Enable));
  Multiplexer multiplexer_3 (.in0(Data_In[2]), .in1(Data_In[3]), .out(Data_Out[2]), .sel(Shift_Enable));
  Multiplexer multiplexer_4 (.in0(Data_In[3]), .in1(1'b0), .out(Data_Out[3]), .sel(Shift_Enable));
endmodule

module FourBitBarrelRightShifter (
  input  [3:0] Data_In,
  input  [1:0] Shift_Amount,
  output [3:0] Data_Out
);

  wire [3:0] shift_stage_1_data_out;

  Shift_Stage shift_stage_1 (.Data_In(Data_In), .Shift_Enable(Shift_Amount[0]), .Data_Out(shift_stage_1_data_out));
  Shift_By_Two_Stage shift_by_two_stage_1 (
    .Data_In(shift_stage_1_data_out), .Shift_Enable(Shift_Amount[1]), .Data_Out(Data_Out));
endmodule

module Shift_By_Two_Stage (
  input  [3:0] Data_In,
  input  Shift_Enable,
  output [3:0] Data_Out
);

  Multiplexer multiplexer_1 (.in0(Data_In[0]), .in1(Data_In[2]), .out(Data_Out[0]), .sel(Shift_Enable));
  Multiplexer multiplexer_2 (.in0(Data_In[1]), .in1(Data_In[3]), .out(Data_Out[1]), .sel(Shift_Enable));
  Multiplexer multiplexer_3 (.in0(Data_In[2]), .in1(1'b0), .out(Data_Out[2]), .sel(Shift_Enable));
  Multiplexer multiplexer_4 (.in0(Data_In[3]), .in1(1'b0), .out(Data_Out[3]), .sel(Shift_Enable));
endmodule

module SRLatch (
  input  S,
  input  R,
  output Not_Q,
  output Q
);

  nor nor_1 (Not_Q, S, Q);
  nor nor_2 (Q, Not_Q, R);
endmodule

module Register_Bit (
  input  D_in,
  input  CLK,
  input  Load,
  output Q_Out
);

  wire multiplexer_1_out;

  Multiplexer multiplexer_1 (.in0(Q_Out), .in1(D_in), .out(multiplexer_1_out), .sel(Load));
  D_Flip_Flop d_ff_1 (.D(multiplexer_1_out), .clk(CLK), .Q(Q_Out));  // open: Qn, preset, reset
endmodule

module FourBitRegister (
  input  [3:0] Data_In,
  input  Load_Enable,
  output [3:0] Data_Out
);

  wire clock_1_out;

  Clock clock_1 (.out(clock_1_out));
  Register_Bit register_bit_1 (.D_in(Data_In[0]), .CLK(clock_1_out), .Load(Load_Enable), .Q_Out(Data_Out[0]));
  Register_Bit register_bit_2 (.D_in(Data_In[1]), .CLK(clock_1_out), .Load(Load_Enable), .Q_Out(Data_Out[1]));
  Register_Bit register_bit_3 (.D_in(Data_In[2]), .CLK(clock_1_out), .Load(Load_Enable), .Q_Out(Data_Out[2]));
  Register_Bit register_bit_4 (.D_in(Data_In[3]), .CLK(clock_1_out), .Load(Load_Enable), .Q_Out(Data_Out[3]));
endmodule
